# Fritzing sketch Esquema_Alimentación y Gestión de Carga (saved by Fritzing 0.9.5d)

parts:
  Módulo_de_carga_TP4056 = TP4056 [chip_label=TP4056 package="DIP (Dual Inline) [THT]"]
  Regulador_de_voltaje_LDO = Voltage Regulator [package=sot23-5]
  ESP32_Wrover = ESP32 DOIT DEVKIT V1 36pin
  Batería_LiPo_3_7V_1200mAh = Battery Holders [package=lipo-1100mAh]
  Interruptor_ON/OFF = Toggle Switch [package=THT]  # not connected

nets:
  N1: Módulo_de_carga_TP4056.pin4, Batería_LiPo_3_7V_1200mAh.+
  N2: Módulo_de_carga_TP4056.pin5, Batería_LiPo_3_7V_1200mAh.-
  N3: Regulador_de_voltaje_LDO.OUT, ESP32_Wrover.Pin_19

notes:
  Bloque de Alimentación y Gestión de carga

custom parts:
  TP4056: A DIP stand-in part for whatever IC you want. With 6 pins on a 300mil dual inline package (DIP) footprint.
  ESP32 DOIT DEVKIT V1 36pin: ESP32 DOIT DEVKIT V1 36pin.
