# Fritzing sketch Esquema_Dispositivo_terminado (saved by Fritzing 0.9.5d)

parts:
  ESP32_Wrover = ESP32 DOIT DEVKIT V1 36pin
  Pantalla_TFT = Nokia 6100 Color LCD [package=nokia6100_lcd]  # not connected
  Batería_LiPo_3_7V = Battery Holders [package=lipo-1100mAh]  # not connected
  TP4056 = TP4056 [chip_label=TP4056 package="DIP (Dual Inline) [THT]"]  # not connected
  LDO = Voltage Regulator LDO [package=sc70]  # not connected
  MAX4466 = Breakout Board for Electret Microphone  # not connected
  Pulsador_arriba = Pushbutton [package="[SMD]"]  # not connected
  Pulsador_abajo = Pushbutton [package="[SMD]"]  # not connected
  Pulsador_seleccionar = Pushbutton [package="[SMD]"]  # not connected
  Pulsador_atrás = Pushbutton [package="[SMD]"]  # not connected
  Pulsador_Tap_Tempo = SWITCH-MOMENTARY-2 [package=tactile-pth-12mm]  # not connected
  Altavoz = Piezo Speaker
  LED_Bemol = LED - 3mm [color="Red (633nm)" package="3 mm [THT]"]
  LED_OK = LED - 3mm [color="Red (633nm)" package="3 mm [THT]"]
  LED_SOS = LED - 3mm [color="Red (633nm)" package="3 mm [THT]"]
  R1 = Resistor [tolerance=±5% resistance=220 package="2010 [SMD]"]
  R2 = Resistor [tolerance=±5% resistance=220 package="0603 [SMD]"]
  R3 = Resistor [tolerance=±5% resistance=220 package="0603 [SMD]"]

nets:
  N1: ESP32_Wrover.Pin_2, ESP32_Wrover.Pin_6, LED_SOS.anode
  N2: ESP32_Wrover.Pin_25, Altavoz.pin2
  N3: LED_Bemol.cathode, R3.Pin_1
  N4: LED_OK.cathode, R1.Pin_1
  N5: LED_SOS.cathode, R2.Pin_1

notes:
  Circuito del dispositivo: Afinador Portátil basado en ESP32

custom parts:
  ESP32 DOIT DEVKIT V1 36pin: ESP32 DOIT DEVKIT V1 36pin.
  TP4056: A DIP stand-in part for whatever IC you want. With 6 pins on a 300mil dual inline package (DIP) footprint.
